# Fritzing sketch ACRModem (saved by Fritzing 0.9.3b)
stripboards: 1

parts:
  U2 = atmega328 [package=dip]
  J1 = female pin header, 2 pins [form="♀ (female)"]
  J4 = female pin header, 2 pins [form="♀ (female)"]
  J5 = female pin header, 2 pins [form="♀ (female)"]
  J6 = female pin header, 2 pins [form="♀ (female)"]
  C1 = Ceramic Capacitor [capacitance=100nF package="100 mil [THT, multilayer]"]
  R2 = Resistor [tolerance=±5% resistance=47k package=THT]
  R3 = Resistor [tolerance=±5% resistance=2.2k package=THT]
  R5 = Resistor [tolerance=±5% resistance=10k package=THT]
  R6 = Resistor [tolerance=±5% resistance=10k package=THT]
  R7 = Resistor [tolerance=±5% resistance=1M package=THT]
  R8 = Resistor [tolerance=±5% resistance=100k package=THT]
  R9 = Resistor [tolerance=±5% resistance=10k package=THT]
  TRS1 = Audio Jack (TRS) 3.5mm [package="PG203J [THT]"]
  C4 = Ceramic Capacitor [capacitance=100nF package="100 mil [THT, multilayer]"]
  R4 = Resistor [tolerance=±5% resistance=1k package=THT]
  J3 = female pin header, 2 pins [form="♀ (female)"]
  TRS2 = Audio Jack (TRS) 3.5mm [package="PG203J [THT]"]
  C5 = Ceramic Capacitor [capacitance=100nF package="100 mil [THT, multilayer]"]
  C3 = Ceramic Capacitor [capacitance=100nF package="100 mil [THT, multilayer]"]
  R10 = Resistor [tolerance=±5% resistance=150 package=THT]
  J7 = female pin header, 2 pins [form="♀ (female)"]
  LED1 = LED - 5mm [color="Red (633nm)" package="5 mm [THT]"]
  U1 = LM 358 Dual Op-Amp [package="DIP8 [THT]"]
  C6 = Ceramic Capacitor [capacitance=19nF package="200 mil [THT, multilayer]"]

nets:
  N1: U2.RESET, C1.1, R9.Pin_0
  N2: U2.D0_(RX), U2.D3_(PWM), J3.pin1
  N3: U2.D1_(TX), J4.pin2
  N4: U2.D2, J7.pin1
  N5: U2.D4, R10.Pin_1
  N6: U2.VCC, U2.AVCC, J1.pin1, J5.pin2, R6.Pin_0, R9.Pin_1, C5.1, U1.connector7
  N7: U2.GND, J1.pin2, J5.pin1, R3.Pin_1, R5.Pin_0, R7.Pin_0, TRS1.Sleeve, C4.0, TRS2.Sleeve, C5.0, LED1.cathode, U1.connector3, C6.1
  N8: U2.D8, U1.connector0
  N9: U2.D11_(PWM), R2.Pin_1
  N10: U2.A4, J6.pin2
  N11: J4.pin1, C1.0
  N12: R2.Pin_0, R3.Pin_0, TRS1.Ring, TRS1.Tip, C4.1
  N13: R5.Pin_1, R6.Pin_1, R8.Pin_0, U1.connector2
  N14: R7.Pin_1, R8.Pin_1, R4.Pin_1, U1.connector1
  N15: R4.Pin_0, C3.0, C6.0
  N16: TRS2.Tip, C3.1
  N17: R10.Pin_0, LED1.anode

// code stored in the sketch: modem.ino
// Modulator/Demodulator for 300 baud Altair cassette interface

#define PIN_SERIAL_IN   2  // must be 2 or 3 (uses interrupt pin INT0 or INT1)
#define PIN_SERIAL_OUT A4  // can be any pin
#define PIN_AUDIO_IN    8  // must be  8 (hardwired ICP1 for timer1)
#define PIN_AUDIO_OUT  11  // must be 11 (hardwired OC2A for timer2)
#define PIN_LED         4  // can be any pin

// timing values for audio output
#define OCRA_1850HZ   135
#define OCRA_2400HZ   104

// timing values for audio input
#define PERIOD_MAX_US 2000  // 1000Hz = 2000 microseconds
#define PERIOD_MID_US  471  // 2125Hz =  471 microseconds
#define PERIOD_MIN_US  333  // 3000Hz =  333 microseconds

// number of good audio pulses in a row required before entering "send" mode
#define NUM_GOOD_PULSES 100

// number of bad audio pulses in a row required before exiting "send" mode
// at 300 baud and audio frequencies of 1850 and 2400Hz, one bit is made up
// of 6-8 pulses. So if we just keep outputting the previous bit value then
// one or two bad pulses may not result in a receive error.
#define NUM_BAD_PULSES  1


// are we in "send" mode?
volatile bool send_data = false;


void got_pulse(bool good)
{
 static volatile byte good_pulses = 0, bad_pulses = 0;

 if( good )
  {
    bad_pulses = 0;
    if( good_pulses<NUM_GOOD_PULSES ) 
      {
        good_pulses++;
        if( good_pulses==NUM_GOOD_PULSES ) 
          { 
            digitalWrite(PIN_LED, HIGH); 
            send_data = true; 
          }
      }
  }
 else if( bad_pulses<NUM_BAD_PULSES )
    {
      bad_pulses++;
      if( bad_pulses==NUM_BAD_PULSES )
        {
          good_pulses = 0;    
          if( send_data )
          {
            digitalWrite(PIN_LED, LOW); 
            digitalWrite(PIN_SERIAL_OUT, HIGH);
            send_data = false;
          }
        }
    }
}


void serial_in_change()
{
  bool data = digitalRead(PIN_SERIAL_IN);
  
  // set audio out frequency depending on serial input
  OCR2A = data ? OCRA_2400HZ : OCRA_1850HZ;  

  // forward data to pin 1 (external serial out)
  PORTD = (PORTD & ~0x02) | (data ? 0x02 : 0);
}


void extern_serial_in_change()
{
  // if not currently converting audio to serial then 
  // forward pin 1 (external serial in) to serial out
  if( !send_data ) digitalWrite(PIN_SERIAL_OUT, PIND & 0x01);
}


ISR(TIMER1_CAPT_vect) 
{ 
  // reset timer 
  TCNT1 = 0;

  // reset output compare A interrupt in case it occurred simultaneously
  TIFR1 = bit(OCF1A);

  // timer ticks equals microseconds since previous rising edge
  // (8Mz clock with prescaler 8 => 1 microsecond per tick)
  unsigned int ticks = ICR1;

  if( ticks<PERIOD_MIN_US )
    got_pulse(false); // short pulse => bad pulse
  else 
    {
      // detected good pulse - we can't get here with ticks>PERIOD_MAX_US
      // because the COMPA interrupt would have been triggered before that
      got_pulse(true);
      if( send_data ) digitalWrite(PIN_SERIAL_OUT, ticks<PERIOD_MID_US);
    }
}


ISR(TIMER1_COMPA_vect)
{  
  // reset timer 
  TCNT1 = 0;

  // reset input capture interrupt in case it occurred simultaneously
  TIFR1 = bit(ICF1);
  ICR1  = 0;
  
  // we haven't seen a rising edge for PERIOD_MAX_US microseconds => bad pulse
  got_pulse(false);
}


void setup() 
{
  // calibration for internal oscillator (not necessary if using crystal)
  // change value such that output square wave on pin 11 is close to 
  // 2400Hz when NOT sending any serial data
  OSCCAL = 0x8e;

  // set up timer2 to produce 1850/2400Hz output wave on OC2A (pin 11)
  TCCR2A = bit(COM2A0) | bit(COM2B1) | bit(WGM20);
  TCCR2B = bit(WGM22) | 2;
  OCR2A  = OCRA_2400HZ;

  // set up serial input to create an interrupt on signal change
  pinMode(PIN_SERIAL_IN, INPUT_PULLUP);
  attachInterrupt(digitalPinToInterrupt(PIN_SERIAL_IN), serial_in_change, CHANGE);

  // set up timer1 to create an input capture interrupt when detecting a 
  // rising edge at the ICP1 input (pin 8) or when reaching PERIOD_MAX_US
  TCCR1A = 0;  
  TCCR1B = bit(ICNC1) | bit(ICES1) | bit(CS11); // enable input capture noise canceler, select rising edge and prescaler 8
  TCCR1C = 0;  
  OCR1A  = PERIOD_MAX_US; // set up for output compare match A after PERIOD_MAX_US microseconds
  TIMSK1 = bit(ICF1) | bit(OCIE1A); // enable interrupts on input capture and output compare match A

  // set up serial output
  pinMode(PIN_SERIAL_OUT, OUTPUT);
  digitalWrite(PIN_SERIAL_OUT, HIGH);

  // set up audio output
  pinMode(PIN_AUDIO_OUT, OUTPUT);

  // set up LED to signal whether we are receiving good data from audio
  pinMode(PIN_LED, OUTPUT);
  digitalWrite(PIN_LED, LOW);

  // set up pin 0/1 for forwarding between main and external serial
  // pin 0 must be connected to pin 3
  pinMode(0, INPUT_PULLUP);
  pinMode(1, OUTPUT);
  digitalWrite(1, HIGH);
  attachInterrupt(digitalPinToInterrupt(3), extern_serial_in_change, CHANGE);
}


void loop() 
{/* nothing to do here */}
